# Fritzing sketch Untitled Sketch (saved by Fritzing 0.9.3b)
breadboards: 1

parts:
  Composant1 = Arduino Uno (Rev3)
  R1 = Resistor [tolerance=±5% resistance=10k package="2512 [SMD]"]
  L1 = Inductor [inductance=10mH package="1206 [SMD]"]
  C1 = Electrolytic Capacitor [capacitance=10nF voltage=5V package="1010 [SMD, electrolytic]"]  # not connected
  R2 = Resistor [tolerance=±5% resistance=3.3k package="2512 [SMD]"]
  D1 = Diode [package=diode-hv]
  R3 = Resistor [tolerance=±5% resistance=1M package="2512 [SMD]"]
  C2 = Electrolytic Capacitor [capacitance=1000μF package="1010 [SMD, electrolytic]"]

nets:
  N1: Composant1.A0, D1.C, R3.Pin_1, C2.-
  N2: Composant1.D9_PWM, R1.Pin_1
  N3: Composant1.GND, R2.Pin_0, R3.Pin_0, C2.+
  N4: R1.Pin_0, L1.pin_1, R2.Pin_1
